# Fritzing sketch Fritzing (saved by Fritzing 0.9.3b)

parts:
  Reg1 = DC-DC CONVERTER [part_number=80633 package=dc-dc_converter]
  Part2 = Arduino Uno (Rev3)
  JACK2 = 2.1mm Barrel Jack with Terminal Block
  KY-3 = Keyes Relay [package=THT]
  PS1 = prefix0000 [part_number=S-350-60]
  SIM800L_BO1 = SIM800L BO
  LED1 = LEDs [package=led10mm]

nets:
  N1: Reg1.OUT-, SIM800L_BO1.GND
  N2: Reg1.OUT+, SIM800L_BO1.ANT, SIM800L_BO1.VCC
  N3: Part2.D13/SCK, KY-3.ground
  N4: Part2.D2, SIM800L_BO1.TX
  N5: Part2.D3_PWM, SIM800L_BO1.RST, SIM800L_BO1.RX
  N6: Part2.5V, KY-3.signal
  N7: JACK2.POS, PS1.connector1
  N8: KY-3.power, PS1.connector3
  N9: KY-3.NO, LED1.C

notes:
  Lampu
  Hubungan ke PLN
  Urutan koneksi
  VCC - GND - IN
  Beberapa PSU kadang urutannya berbeda.
  Jadi perhatikan Simbol pada power supply
  Atur dulu sampai output 3,7V baru hubungkan ke sim800l
  Urutan pin SIM yg konek
  VCC
  RX
  TX
  GND

custom parts:
  DC-DC CONVERTER: WYHP 5A constant current/voltage manufactured by Shenzhen Weiyapuhua Technology Co., Ltd
  Keyes Relay: The Keyes 5V relay module is suitable for SCM development, home appliance control. It uses a 5V~12V TIL control signal which can control DC / AC signal.
  LEDs: LEDs Standard schematic elements and footprints for 5mm, 3mm, 1206, and 0603 sized LEDs. 5mm - Spark Fun Electronics SKU : COM-00529 (and others)
